# Fritzing sketch rpi_wiring_schematic (saved by Fritzing 0.9.2b)
breadboards: 1

parts:
  Raspberry_Pi_1 = Raspberry Pi 3 [part_number=RPI-3-V1.2]
  Part1 = Adafruit LSM9DS1 9DoF Breakout [part_number="Adafruit #3387"]

nets:
  N1: Raspberry_Pi_1.GIPO10, Part1.SDA
  N2: Raspberry_Pi_1.GIPO9, Part1.SDO_M, Part1.SDO_AG
  N3: Raspberry_Pi_1.GIPO11, Part1.SCL
  N4: Raspberry_Pi_1.GIPO7, Part1.CS_MAG
  N5: Raspberry_Pi_1.GIPO8, Part1.CS_AG
  GND: Raspberry_Pi_1.GND, Part1.GND
  5V: Raspberry_Pi_1.5V, Part1.VIN

custom parts:
  Adafruit LSM9DS1 9DoF Breakout: Add motion, direction and orientation sensing to your Arduino project with this all-in-one 9-DOF sensor. Inside the chip are three sensors, one is a classic 3-axis accelerometer, which can tell you which direction is down towards the Earth (by measuring gravity) or how fast the board is accelerating in 3D space. The other is a 3-axis magnetometer that can sense where the strongest magnetic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
